# Fritzing sketch Untitled Sketch (saved by Fritzing 0.9.3b)

parts:
  Componente2 = Arduino Uno (Rev3)
  M2 = DC Motor
  S1 = H-Bridge with L298N
  S2 = H-Bridge with L298N
  A1 = Electropeak 2.4in LCD
  Componente3 = Arduino Mega 2560 (Rev3)
  M4 = DC Motor
  M3 = DC Motor
  M5 = DC Motor

nets (from the breadboard view):
  N1: Componente2.D13/SCK, Componente3.D31
  GND: Componente2.GND, A1.Pin_4, A1.Pin_5, Componente3.GND
  N2: Componente2.D0/RX, S1.IN4
  N3: Componente2.D1/TX, S1.IN3
  N4: Componente2.D2, S1.IN2
  N5: Componente2.D3_PWM, S1.IN1
  N6: Componente2.D4, S2.IN4
  N7: Componente2.D5_PWM, S2.IN3
  N8: Componente2.D6_PWM, S2.IN2
  N9: Componente2.D7, S2.IN1
  N10: M2.pin_1, S2.M2-01
  N11: M2.pin_2, S2.M2-02
  N12: S1.M1-01, M4.pin_2
  N13: S1.M1-02, M4.pin_1
  N14: S1.M2-01, M3.pin_1
  N15: S1.M2-02, M3.pin_2
  N16: S2.M1-01, M5.pin_2
  N17: S2.M1-02, M5.pin_1
  N18: A1.Pin_1, Componente3.RESET
  N19: A1.Pin_2, Componente3.3V3
  N20: A1.Pin_3, Componente3.5V
  N21: A1.Pin_6, Componente3.VIN
  N22: A1.Pin_7, Componente3.A0
  N23: A1.Pin_8, Componente3.A1
  N24: A1.Pin_9, Componente3.A2
  N25: A1.Pin_10, Componente3.A3
  N26: A1.Pin_11, Componente3.A4
  N27: A1.Pin_12, Componente3.A5
  N28: A1.Pin_13, Componente3.D0_RX0
  N29: A1.Pin_14, Componente3.D1_TX0
  N30: A1.Pin_15, Componente3.D2_PWM
  N31: A1.Pin_16, Componente3.D3_PWM
  N32: A1.Pin_17, Componente3.D4_PWM
  N33: A1.Pin_18, Componente3.D5_PWM
  N34: A1.Pin_19, Componente3.D6_PWM
  N35: A1.Pin_20, Componente3.D7_PWM
  N36: A1.Pin_21, Componente3.D8_PWM
  N37: A1.Pin_22, Componente3.D9_PWM
  N38: A1.Pin_23, Componente3.D10_PWM
  N39: A1.Pin_24, Componente3.D11_PWM
  N40: A1.Pin_25, Componente3.D12_PWM

custom parts:
  H-Bridge with L298N: h-bridge
  Electropeak 2.4in LCD: 2.4 inch Touch TFT LCD Display Shield for Arduino UNO/Mega.
